# Fritzing sketch IV_scheme (saved by Fritzing 0.9.3b)
breadboards: 1

parts:
  Part1 = Arduino Due (Rev2b)
  R1 = Resistor [tolerance=±5% resistance=220 package=THT]
  LED1 = LED - 5mm [color="Red (633nm)" package="5 mm [THT]"]

nets:
  N1: Part1.DAC0, LED1.anode
  N2: Part1.A0, R1.Pin_1, LED1.cathode
  N3: Part1.GND, R1.Pin_0
